// Logisim project CPU2.circ as structural Verilog: 1 circuit, main circuit main
module main (
  input  in_1
);

  wire ALU_A_SIGNED, ALU_A_WRITE, big_rom_1_p1, CLK, HALT, PROG_NEXT, PROG_REG_WRITE, pull_resistor_1_node,
       pull_resistor_2_node, SAVE_IR;
  wire [4:0] ALU_A_LEFT_ADDR, ALU_A_OP, ALU_A_OUTPUT_ADDR, ALU_A_RIGHT_ADDR, PROG_REG_ADDR;
  wire [7:0] controlled_buffer_1_out, counter_2_q, IR_q, pull_resistor_3_node;
  wire [15:0] counter_1_q;
  wire [23:0] IR_q_2;
  wire [31:0] ALU_A_LEFT, ALU_A_OUTPUT, ALU_A_RIGHT, PROG_VALUE;

  Clock clock_1 (.out(CLK));
  ROM #(.addrWidth(16), .dataWidth(32)) PROG (.addr(counter_1_q), .data(PROG_VALUE));
  Counter #(.width(16), .max('hffff)) counter_1 (
    .up(pull_resistor_1_node), .count(PROG_NEXT), .clk(CLK), .Q(counter_1_q));  // open: clr, load, D, carry
  Pull_Resistor #(.pull(1)) pull_resistor_1 (.node(pull_resistor_1_node));
  Counter counter_2 (
    .load(SAVE_IR), .up(pull_resistor_2_node), .count(pull_resistor_2_node), .clk(CLK),
    .D(pull_resistor_3_node), .Q(counter_2_q));  // open: clr, carry
  Pull_Resistor #(.pull(1)) pull_resistor_2 (.node(pull_resistor_2_node));
  Pull_Resistor pull_resistor_3 (.node(pull_resistor_3_node));
  Register #(.width(32)) IR (.D(PROG_VALUE), .en(SAVE_IR), .clk(CLK), .Q({IR_q, IR_q_2}));  // open: clr
  assign controlled_buffer_1_out = in_1 ? counter_2_q : 8'bz;  // Controlled_Buffer controlled_buffer_1
  // Big_ROM #(.addressWidth(40)) big_rom_1: pin names not known; wires that end beside it: big_rom_1_p1, IR_q
  // Splitter #(.fanout(32), .incoming(32), .appear("right"), .spacing("double")) splitter_1: pin names not known; wires that end beside it: big_rom_1_p1, HALT, SAVE_IR, PROG_NEXT
  // Splitter #(.fanout(5), .incoming(5), .appear("center"), .spacing("double")) splitter_2: pin names not known; wires that end beside it: PROG_REG_WRITE, PROG_REG_ADDR
  // Splitter #(.fanout(5), .incoming(5), .appear("center"), .spacing("double")) splitter_3: pin names not known; wires that end beside it: ALU_A_LEFT_ADDR
  // Splitter #(.fanout(5), .incoming(5), .appear("center"), .spacing("double")) splitter_4: pin names not known; wires that end beside it: ALU_A_RIGHT_ADDR
  // Splitter #(.fanout(5), .incoming(5), .appear("center"), .spacing("double")) splitter_5: pin names not known; wires that end beside it: ALU_A_OUTPUT_ADDR
  // Splitter #(.fanout(5), .incoming(5), .appear("center"), .spacing("double")) splitter_6: pin names not known; wires that end beside it: ALU_A_SIGNED, ALU_A_WRITE, ALU_A_OP
  // ALU #(.width(32)) alu_1: pin names not known; wires that end beside it: ALU_A_SIGNED, ALU_A_OP, ALU_A_LEFT, ALU_A_RIGHT, ALU_A_OUTPUT
  // Register_Bank #(.width(32), .registerCount(32), .portCount(4)) register_bank_1: pin names not known; wires that end beside it: ALU_A_OUTPUT_ADDR, ALU_A_RIGHT_ADDR, ALU_A_LEFT_ADDR, PROG_REG_ADDR, CLK, ALU_A_WRITE, ALU_A_OUTPUT, PROG_REG_WRITE, PROG_VALUE, ALU_A_RIGHT, ALU_A_LEFT

  // Notes on the sheet:
  //   contents of PROG (hex, n*v repeats v):
  //   100000 1 100001 2 20000a
endmodule
